# Fritzing sketch F9D1YMMIVA4KQL4 (saved by Fritzing 0.9.2b)

parts:
  e-radionica1 = TCS230 Color Sensor [part_number=101209]
  Onderdeel1 = Arduino Uno (Rev3) - ICSP

nets:
  GND: e-radionica1.Gnd, Onderdeel1.GND
  N1: e-radionica1.S1, Onderdeel1.D4
  N2: e-radionica1.S0, Onderdeel1.D3_PWM
  N3: e-radionica1.S3, Onderdeel1.D6_PWM
  N4: e-radionica1.S2, Onderdeel1.D5_PWM
  N5: e-radionica1.Out, Onderdeel1.D2
  VCC: e-radionica1.Vcc, Onderdeel1.5V

notes:
  Author: Danny van den Brande

custom parts:
  TCS230 Color Sensor: TCS230
